// Logisim project 1st canonical form(min).circ as structural Verilog: 1 circuit, main circuit main
module main (
  input  C,
  input  A,
  input  B,
  output a_2,
  output b_2,
  output c___AC_prime___B_prime_C_prime,
  output d,
  output out_8,
  output f____A_prime_B_prime___BC_prime,
  output g___AB___C
);

  wire and_1_out, and_2_out, and_3_out, and_4_out, and_5_out, and_6_out, and_7_out, not_1_out, not_2_out,
       not_3_out, not_4_out, not_5_out, not_6_out, not_7_out, not_8_out, not_9_out, not_10_out;

  not not_1 (not_1_out, A);
  not not_2 (not_2_out, B);
  not not_3 (not_3_out, C);
  not not_4 (not_4_out, A);
  not not_5 (not_5_out, B);
  and and_1 (and_1_out, not_1_out, not_2_out);
  and and_2 (and_2_out, B, not_3_out);
  not not_6 (not_6_out, C);
  not not_7 (not_7_out, C);
  or or_1 (a_2, not_4_out, B);
  and and_3 (and_3_out, not_5_out, not_6_out);
  and and_4 (and_4_out, B, C);
  and and_5 (and_5_out, A, not_7_out);
  not not_8 (not_8_out, B);
  not not_9 (not_9_out, C);
  not not_10 (not_10_out, A);
  or or_2 (f____A_prime_B_prime___BC_prime, and_1_out, and_2_out);
  and and_6 (and_6_out, not_8_out, not_9_out);
  not not_11 (out_8, A);
  or or_3 (b_2, and_3_out, and_4_out);
  or or_4 (d, not_10_out, B);
  or or_5 (c___AC_prime___B_prime_C_prime, and_5_out, and_6_out);
  and and_7 (and_7_out, A, B);
  or or_6 (g___AB___C, and_7_out, C);
  _7_Segment_Display u_7_segment_display_1 (
    .g(g___AB___C), .f(f____A_prime_B_prime___BC_prime), .a(a_2), .b(b_2), .e(out_8), .d(d),
    .c(c___AC_prime___B_prime_C_prime));  // open: dp

  // Notes on the sheet:
  //   a = A' + B
  //   b = B'C' + BC
  //   e = A'
  //                      d = A' + B
  //                         Enter Your Inputs : 
endmodule
