// Logisim project 2nd canonical form.circ as structural Verilog: 1 circuit, main circuit main
module main (
  input  A,
  input  B,
  input  C
);

  wire and_1_out, and_2_out, and_3_out, and_4_out, and_5_out, and_6_out, and_7_out, not_1_out, not_2_out,
       not_3_out, not_4_out, not_5_out, not_6_out, not_7_out, not_8_out, not_9_out, not_10_out, not_11_out,
       not_12_out, not_13_out, not_14_out, not_15_out, not_16_out, not_17_out, not_18_out, not_19_out,
       not_20_out, not_21_out, not_22_out, not_23_out, not_24_out, not_25_out, not_26_out, not_27_out,
       not_28_out, not_29_out, not_30_out, or_1_out, or_2_out, or_3_out, or_4_out, or_5_out, or_6_out,
       or_7_out, or_8_out, or_9_out, or_10_out, or_11_out, or_12_out, or_13_out, or_14_out, or_15_out,
       or_16_out, or_17_out, or_18_out, or_19_out, or_20_out;

  not not_1 (not_1_out, A);
  not not_2 (not_2_out, C);
  not not_3 (not_3_out, C);
  not not_4 (not_4_out, A);
  not not_5 (not_5_out, A);
  not not_6 (not_6_out, B);
  not not_7 (not_7_out, C);
  or or_1 (or_1_out, not_1_out, B, B);
  not not_8 (not_8_out, A);
  not not_9 (not_9_out, C);
  or or_2 (or_2_out, A, B, not_2_out);
  not not_10 (not_10_out, B);
  or or_3 (or_3_out, A, B, not_3_out);
  not not_11 (not_11_out, B);
  or or_4 (or_4_out, not_4_out, B, C);
  not not_12 (not_12_out, A);
  not not_13 (not_13_out, C);
  or or_5 (or_5_out, not_5_out, B, C);
  not not_14 (not_14_out, C);
  or or_6 (or_6_out, A, not_6_out, not_7_out);
  or or_7 (or_7_out, A, not_15_out, C);
  not not_15 (not_15_out, B);
  not not_16 (not_16_out, A);
  or or_8 (or_8_out, not_8_out, B, not_9_out);
  or or_9 (or_9_out, A, not_10_out, C);
  not not_17 (not_17_out, C);
  or or_10 (or_10_out, A, not_11_out, C);
  not not_18 (not_18_out, C);
  or or_11 (or_11_out, not_12_out, B, not_13_out);
  not not_19 (not_19_out, A);
  or or_12 (or_12_out, not_19_out, B, not_14_out);
  not not_20 (not_20_out, B);
  not not_21 (not_21_out, A);
  or or_13 (or_13_out, not_21_out, B, C);
  not not_22 (not_22_out, C);
  or or_14 (or_14_out, not_16_out, B, C);
  not not_23 (not_23_out, A);
  not not_24 (not_24_out, B);
  not not_25 (not_25_out, A);
  not not_26 (not_26_out, A);
  and and_1 (and_1_out, or_1_out, or_8_out);
  not not_27 (not_27_out, A);
  or or_15 (or_15_out, not_23_out, B, not_17_out);
  not not_28 (not_28_out, B);
  not not_29 (not_29_out, A);
  or or_16 (or_16_out, A, not_24_out, not_18_out);
  not not_30 (not_30_out, C);
  and and_2 (and_2_out, or_4_out, or_11_out);
  or or_17 (or_17_out, not_25_out, not_20_out, C);
  or or_18 (or_18_out, not_26_out, B, not_22_out);
  and and_3 (and_3_out, or_7_out, or_14_out);
  or or_19 (or_19_out, not_27_out, not_28_out, C);
  or or_20 (or_20_out, not_29_out, B, not_30_out);
  and and_4 (and_4_out, or_2_out, or_9_out, or_15_out, or_19_out);
  and and_5 (and_5_out, or_3_out, or_10_out, or_16_out, or_20_out);
  and and_6 (and_6_out, or_5_out, or_12_out, or_17_out);
  and and_7 (and_7_out, or_6_out, or_13_out, or_18_out);
  _7_Segment_Display u_7_segment_display_1 (
    .g(and_3_out), .f(and_7_out), .a(and_1_out), .b(and_4_out), .e(and_6_out), .d(and_2_out), .c(and_5_out));  // open: dp
endmodule
