// Logisim project 2nd canonical(min).circ as structural Verilog: 1 circuit, main circuit main
module main (
  input  A,
  input  B,
  input  C
);

  wire and_1_out, and_2_out, and_3_out, and_4_out, not_1_out, not_2_out, not_3_out, not_4_out, not_5_out,
       not_6_out, not_7_out, not_8_out, not_9_out, or_1_out, or_2_out, or_3_out, or_4_out, or_5_out,
       or_6_out, or_7_out, or_8_out;

  not not_1 (not_1_out, A);
  not not_2 (not_2_out, B);
  not not_3 (not_3_out, C);
  not not_4 (not_4_out, A);
  not not_5 (not_5_out, B);
  not not_6 (not_6_out, C);
  not not_7 (not_7_out, C);
  not not_8 (not_8_out, A);
  not not_9 (not_9_out, A);
  or or_1 (or_1_out, not_1_out, B);
  or or_2 (or_2_out, not_2_out, not_3_out);
  or or_3 (or_3_out, A, C);
  or or_4 (or_4_out, B, C);
  or or_5 (or_5_out, not_4_out, B);
  or or_6 (or_6_out, not_5_out, C);
  or or_7 (or_7_out, B, not_6_out);
  or or_8 (or_8_out, not_8_out, B);
  and and_1 (and_1_out, or_6_out, or_7_out);
  and and_2 (and_2_out, A, not_7_out);
  and and_3 (and_3_out, or_1_out, or_2_out);
  and and_4 (and_4_out, or_3_out, or_4_out);
  _7_Segment_Display u_7_segment_display_1 (
    .g(and_4_out), .f(and_3_out), .a(or_5_out), .b(and_1_out), .e(not_9_out), .d(or_8_out), .c(and_2_out));  // open: dp
endmodule
