// Logisim project DFF-sequential-logic-design.circ as structural Verilog: 1 circuit, main circuit main
module main (
  input  in_1
);

  wire A, A_prime, a_t, and_1_out, and_2_out, and_3_out, and_4_out, and_5_out, and_6_out, and_7_out,
       and_8_out, and_9_out, and_10_out, and_11_out, and_12_out, and_13_out, and_14_out, B, B_prime, b_t, C,
       C_prime, c_t, CLK, DA, DB, DC, e, f, FA, FC, g, I_prime, nand_1_out, nand_2_out, nand_3_out,
       nand_4_out, nand_5_out, nand_6_out, nand_7_out, nand_8_out, nand_10_out, nand_12_out;

  Clock clock_1 (.out(CLK));
  and and_1 (and_1_out, A_prime, B_prime, C_prime);
  and and_2 (and_2_out, A, C);
  and and_3 (and_3_out, A, B);
  and and_4 (and_4_out, A, C_prime);
  and and_5 (and_5_out, A_prime, C);
  not not_1 (I_prime, in_1);
  or or_1 (FA, and_1_out, and_2_out);
  or or_2 (FC, and_3_out, and_4_out, and_5_out);
  _7_Segment_Display u_7_segment_display_1 (.g(g), .f(f), .a(a_t), .b(b_t), .e(e), .d(a_t), .c(c_t));  // open: dp
  D_Flip_Flop d_ff_1 (.clk(CLK), .D(DA), .Q(A), .Qn(A_prime));  // open: preset, en, reset
  D_Flip_Flop d_ff_2 (.clk(CLK), .D(DB), .Q(B), .Qn(B_prime));  // open: preset, en, reset
  D_Flip_Flop d_ff_3 (.clk(CLK), .D(DC), .Q(C), .Qn(C_prime));  // open: preset, en, reset
  nand nand_1 (nand_1_out, C_prime, C_prime);
  nand nand_2 (nand_2_out, FC, FC);
  nand nand_3 (nand_3_out, FA, FA);
  nand nand_4 (nand_4_out, C_prime, FC);
  nand nand_5 (nand_5_out, FA, nand_2_out);
  nand nand_6 (nand_6_out, nand_3_out, nand_1_out);
  nand nand_7 (nand_7_out, FA, C_prime);
  nand nand_8 (nand_8_out, FC, FC);
  nand nand_9 (a_t, FA, nand_1_out);
  nand nand_10 (nand_10_out, nand_1_out, nand_2_out);
  nand nand_11 (c_t, nand_5_out, nand_5_out);
  nand nand_12 (nand_12_out, C_prime, nand_2_out);
  nand nand_13 (g, nand_7_out, nand_8_out);
  and and_6 (and_6_out, in_1, A);
  and and_7 (and_7_out, A, B);
  and and_8 (and_8_out, A, c_t);
  and and_9 (and_9_out, I_prime, A_prime, B_prime, C_prime);
  nand nand_14 (b_t, nand_10_out, nand_4_out);
  nand nand_15 (e, FA, FA);
  nand nand_16 (f, nand_6_out, nand_12_out);
  or or_3 (DA, and_6_out, and_7_out, and_8_out, and_9_out);
  and and_10 (and_10_out, B, C);
  and and_11 (and_11_out, in_1, B);
  and and_12 (and_12_out, I_prime, B_prime, C_prime);
  and and_13 (and_13_out, in_1, C);
  and and_14 (and_14_out, I_prime, C_prime);
  or or_4 (DC, and_13_out, and_14_out);
  or or_5 (DB, and_10_out, and_11_out, and_12_out);

  // Other names for the same wires on the sheet: d = a_t; FB = C_prime; I = in_1

  // Notes on the sheet:
  //            Enter Your Input : I
  //            OUTPUT LOGIC
  //                                  DRIVING LOGIC
  //                                                COMBINATIONAL LOGIC
  //                                        FF INPUT LOGIC
  //   e
  //   d
  //   c
  //   f
  //   g
  //   a
  //   b
endmodule
