// Logisim project JKFF sequential logic design.circ as structural Verilog: 1 circuit, main circuit main
module main (
  input  in_1,
  output out_2,
  output out_3,
  output out_4
);

  wire A, A_prime, a_t, and_1_out, and_2_out, and_3_out, and_4_out, and_5_out, B, B_prime, b_t, C, c_t, CLK,
       e, f, FA, FC, g, I_prime, JA, JB, nand_1_out, nand_2_out, nand_3_out, nand_4_out, nand_5_out,
       nand_8_out, nand_9_out, nand_10_out, nand_11_out, nand_12_out, nand_13_out, nand_14_out, nand_15_out,
       nand_17_out, nand_19_out;

  Clock clock_1 (.out(CLK));
  and and_1 (and_1_out, A_prime, B_prime, out_3);
  and and_2 (and_2_out, A, C);
  and and_3 (and_3_out, A, B);
  and and_4 (and_4_out, A, out_3);
  and and_5 (and_5_out, A_prime, C);
  nand nand_1 (nand_1_out, A_prime, B_prime, out_3);
  nand nand_2 (nand_2_out, A, C);
  nand nand_3 (nand_3_out, A, B);
  nand nand_4 (nand_4_out, A, out_3);
  nand nand_5 (nand_5_out, A_prime, C);
  not not_1 (I_prime, in_1);
  or or_1 (out_2, and_1_out, and_2_out);
  or or_2 (out_4, and_3_out, and_4_out, and_5_out);
  nand nand_6 (FA, nand_1_out, nand_2_out);
  nand nand_7 (FC, nand_3_out, nand_4_out, nand_5_out);
  _7_Segment_Display u_7_segment_display_1 (.g(g), .f(f), .a(a_t), .b(b_t), .e(e), .d(a_t), .c(c_t));  // open: dp
  J_K_Flip_Flop j_k_ff_1 (.J(JA), .clk(CLK), .K(JA), .Q(A), .Qn(A_prime));  // open: preset, en, reset
  J_K_Flip_Flop j_k_ff_2 (.J(JB), .clk(CLK), .K(JB), .Q(B), .Qn(B_prime));  // open: preset, en, reset
  J_K_Flip_Flop j_k_ff_3 (.J(I_prime), .clk(CLK), .K(I_prime), .Q(C), .Qn(out_3));  // open: preset, en, reset
  nand nand_8 (nand_8_out, out_3, out_3);
  nand nand_9 (nand_9_out, FC, FC);
  nand nand_10 (nand_10_out, FA, FA);
  nand nand_11 (nand_11_out, out_3, FC);
  nand nand_12 (nand_12_out, FA, nand_9_out);
  nand nand_13 (nand_13_out, nand_10_out, nand_8_out);
  nand nand_14 (nand_14_out, FA, out_3);
  nand nand_15 (nand_15_out, FC, FC);
  nand nand_16 (a_t, FA, nand_8_out);
  nand nand_17 (nand_17_out, nand_8_out, nand_9_out);
  nand nand_18 (c_t, nand_12_out, nand_12_out);
  nand nand_19 (nand_19_out, out_3, nand_9_out);
  nand nand_20 (g, nand_14_out, nand_15_out);
  and and_6 (JA, I_prime, B_prime, out_3);
  and and_7 (JB, I_prime, out_3);
  nand nand_21 (b_t, nand_17_out, nand_11_out);
  nand nand_22 (e, FA, FA);
  nand nand_23 (f, nand_13_out, nand_19_out);

  // Other names for the same wires on the sheet: d = a_t; C_prime = out_3; FB = out_3; I = in_1; KA = JA; KB = JB;
  //   JC = I_prime; KC = I_prime

  // Notes on the sheet:
  //            Enter Your Input : I
  //   NAND LOGIC
  //            OUTPUT LOGIC
  //                                  DRIVING LOGIC
  //                                                COMBINATIONAL LOGIC
  //                                        FF INPUT LOGIC
  //   e
  //   d
  //   c
  //   f
  //   g
  //   a
  //   b
endmodule
