// Logisim project Multiplexer.circ as structural Verilog: 1 circuit, main circuit main
module main (
  input  in_1,
  input  in_2,
  input  in_3,
  input  in_4,
  input  in_5,
  input  in_6,
  input  in_7,
  input  in_8,
  input  in_9,
  input  [2:0] Enter_your_Inputs,
  input  in_11,
  input  in_12,
  input  in_13,
  input  in_14,
  input  in_15,
  input  in_16,
  input  in_17,
  input  in_18,
  input  in_19,
  input  in_20,
  input  in_21,
  input  in_22,
  input  in_23,
  input  in_24,
  input  in_25,
  input  in_26,
  input  in_27,
  input  in_28,
  input  in_29,
  input  in_30,
  input  in_31,
  input  in_32,
  input  in_33,
  input  in_34,
  input  in_35,
  input  in_36,
  input  in_37,
  input  in_38,
  input  in_39,
  input  in_40,
  input  in_41,
  input  in_42,
  input  in_43,
  input  in_44,
  input  in_45,
  input  in_46,
  input  in_47,
  input  in_48,
  input  in_49,
  input  in_50,
  input  in_51,
  input  in_52,
  input  in_53,
  input  in_54,
  input  in_55,
  input  in_56,
  input  in_57
);

  wire multiplexer_1_out, multiplexer_2_out, multiplexer_3_out, multiplexer_4_out, multiplexer_5_out,
       multiplexer_6_out, multiplexer_7_out;

  Multiplexer #(.select(3), .enable("false")) multiplexer_1 (
    .in0(in_1), .in1(in_3), .in2(in_5), .in3(in_7), .in4(in_9), .in5(in_12), .in6(in_14), .in7(in_16),
    .out(multiplexer_1_out), .sel(Enter_your_Inputs));
  Multiplexer #(.select(3), .enable("false")) multiplexer_2 (
    .in0(in_18), .in1(in_21), .in2(in_24), .in3(in_27), .in4(in_30), .in5(in_33), .in6(in_36), .in7(in_39),
    .out(multiplexer_2_out), .sel(Enter_your_Inputs));
  Multiplexer #(.select(3), .enable("false")) multiplexer_3 (
    .in0(in_42), .in1(in_43), .in2(in_45), .in3(in_47), .in4(in_49), .in5(in_51), .in6(in_53), .in7(in_55),
    .out(multiplexer_3_out), .sel(Enter_your_Inputs));
  _7_Segment_Display u_7_segment_display_1 (
    .g(multiplexer_4_out), .f(multiplexer_7_out), .a(multiplexer_1_out), .b(multiplexer_5_out),
    .e(multiplexer_3_out), .d(multiplexer_6_out), .c(multiplexer_2_out));  // open: dp
  Multiplexer #(.select(3), .enable("false")) multiplexer_4 (
    .in0(in_19), .in1(in_22), .in2(in_25), .in3(in_28), .in4(in_31), .in5(in_34), .in6(in_37), .in7(in_40),
    .out(multiplexer_4_out), .sel(Enter_your_Inputs));
  Multiplexer #(.select(3), .enable("false")) multiplexer_5 (
    .in0(in_2), .in1(in_4), .in2(in_6), .in3(in_8), .in4(in_11), .in5(in_13), .in6(in_15), .in7(in_17),
    .out(multiplexer_5_out), .sel(Enter_your_Inputs));
  Multiplexer #(.select(3), .enable("false")) multiplexer_6 (
    .in0(in_20), .in1(in_23), .in2(in_26), .in3(in_29), .in4(in_32), .in5(in_35), .in6(in_38), .in7(in_41),
    .out(multiplexer_6_out), .sel(Enter_your_Inputs));
  Multiplexer #(.select(3), .enable("false")) multiplexer_7 (
    .in0(in_44), .in1(in_46), .in2(in_48), .in3(in_50), .in4(in_52), .in5(in_54), .in6(in_56), .in7(in_57),
    .out(multiplexer_7_out), .sel(Enter_your_Inputs));

  // Notes on the sheet:
  //   C
  //   A
  //   E
  //   C
  //   B
  //   A
  //   G
  //   B
  //        D
  //   F
endmodule
