// Logisim project NAND Logic.circ as structural Verilog: 1 circuit, main circuit main
module main (
  input  A,
  input  B,
  input  C
);

  wire nand_1_out, nand_2_out, nand_3_out, nand_4_out, nand_5_out, nand_6_out, nand_7_out, nand_8_out,
       nand_9_out, nand_10_out, nand_11_out, nand_12_out, nand_13_out, nand_14_out, nand_15_out, nand_16_out,
       nand_17_out, not_1_out, not_2_out, not_3_out, not_4_out, not_5_out, not_6_out;

  not not_1 (not_1_out, B);
  not not_2 (not_2_out, C);
  not not_3 (not_3_out, C);
  not not_4 (not_4_out, A);
  not not_5 (not_5_out, B);
  not nand_1 (nand_1_out, B);  // NAND_Gate
  nand nand_2 (nand_2_out, not_1_out, not_2_out);
  nand nand_3 (nand_3_out, B, C);
  nand nand_4 (nand_4_out, A, not_3_out);
  not nand_5 (nand_5_out, B);  // NAND_Gate
  nand nand_6 (nand_6_out, not_4_out, not_5_out);
  not not_6 (not_6_out, C);
  not nand_7 (nand_7_out, nand_4_out);  // NAND_Gate
  not nand_8 (nand_8_out, A);  // NAND_Gate
  nand nand_9 (nand_9_out, A, B);
  nand nand_10 (nand_10_out, A, B);
  nand nand_11 (nand_11_out, A, nand_1_out);
  nand nand_12 (nand_12_out, A, nand_5_out);
  nand nand_13 (nand_13_out, B, not_6_out);
  not nand_14 (nand_14_out, C);  // NAND_Gate
  nand nand_15 (nand_15_out, nand_2_out, nand_3_out);
  nand nand_16 (nand_16_out, nand_6_out, nand_9_out, nand_13_out);
  nand nand_17 (nand_17_out, nand_10_out, nand_14_out);
  _7_Segment_Display u_7_segment_display_1 (
    .g(nand_17_out), .f(nand_16_out), .a(nand_11_out), .b(nand_15_out), .e(nand_8_out), .d(nand_12_out),
    .c(nand_7_out));  // open: dp

  // Notes on the sheet:
  //   c
  //   a
  //   d
  //   e
  //   b
  //   f
  //   g
endmodule
