// Logisim project NOR Logic.circ as structural Verilog: 1 circuit, main circuit main
module main (
  input  A,
  input  B,
  input  C
);

  wire nor_1_out, nor_2_out, nor_3_out, nor_4_out, nor_5_out, nor_6_out, nor_7_out, nor_8_out, nor_9_out,
       nor_10_out, nor_11_out, nor_12_out, nor_13_out, nor_14_out, nor_15_out, nor_16_out, nor_17_out,
       not_1_out, not_2_out, not_3_out, not_4_out, not_5_out, not_6_out, not_7_out, not_8_out;

  not not_1 (not_1_out, C);
  not not_2 (not_2_out, A);
  not not_3 (not_3_out, A);
  not not_4 (not_4_out, B);
  not not_5 (not_5_out, C);
  not not_6 (not_6_out, A);
  not not_7 (not_7_out, B);
  not not_8 (not_8_out, C);
  nor nor_1 (nor_1_out, not_2_out, B);
  nor nor_2 (nor_2_out, not_6_out, B);
  nor nor_3 (nor_3_out, not_7_out, C);
  nor nor_4 (nor_4_out, B, not_8_out);
  not nor_5 (nor_5_out, nor_1_out);  // NOR_Gate
  nor nor_6 (nor_6_out, not_3_out, B);
  nor nor_7 (nor_7_out, not_4_out, not_5_out);
  nor nor_8 (nor_8_out, A, C);
  nor nor_9 (nor_9_out, B, C);
  not nor_10 (nor_10_out, nor_2_out);  // NOR_Gate
  not nor_11 (nor_11_out, A);  // NOR_Gate
  not nor_12 (nor_12_out, not_1_out);  // NOR_Gate
  not nor_13 (nor_13_out, A);  // NOR_Gate
  nor nor_14 (nor_14_out, nor_6_out, nor_7_out);
  nor nor_15 (nor_15_out, nor_3_out, nor_4_out);
  nor nor_16 (nor_16_out, nor_11_out, nor_12_out);
  nor nor_17 (nor_17_out, nor_8_out, nor_9_out);
  _7_Segment_Display u_7_segment_display_1 (
    .g(nor_17_out), .f(nor_14_out), .a(nor_10_out), .b(nor_15_out), .e(nor_13_out), .d(nor_5_out),
    .c(nor_16_out));  // open: dp
endmodule
