// Logisim project ece212-5.circ as structural Verilog: 1 circuit, main circuit main
module main (
  input  in_1,
  input  in_2,
  input  in_3,
  output out_4,
  output out_5,
  output out_6,
  output out_7,
  output out_8,
  output out_9,
  output out_10,
  output out_11
);

  wire and_1_out, and_2_out, and_3_out, and_4_out, and_5_out, and_6_out, not_1_out, not_2_out, not_3_out,
       not_4_out, not_5_out, not_7_out, not_8_out, not_9_out;

  not not_1 (not_1_out, in_3);
  not not_2 (not_2_out, in_1);
  not not_3 (not_3_out, in_2);
  not not_4 (not_4_out, in_3);
  not not_5 (not_5_out, in_1);
  not not_6 (out_10, in_1);
  not not_7 (not_7_out, in_1);
  and and_1 (and_1_out, not_7_out, not_8_out);
  not not_8 (not_8_out, in_2);
  and and_2 (and_2_out, in_1, in_2);
  and and_3 (and_3_out, in_2, not_1_out);
  and and_4 (and_4_out, in_1, in_2);
  and and_5 (and_5_out, not_3_out, not_4_out);
  and and_6 (and_6_out, in_2, in_3);
  not not_9 (not_9_out, in_3);
  or or_1 (out_4, not_2_out, in_2);
  and and_7 (out_6, in_1, not_9_out);
  or or_2 (out_7, not_5_out, in_2);
  or or_3 (out_5, and_5_out, and_6_out);
  or or_4 (out_9, and_1_out, and_2_out, and_3_out);
  or or_5 (out_8, and_4_out, in_3);
  _7_Segment_Display u_7_segment_display_1 (
    .g(out_8), .f(out_9), .a(out_4), .b(out_5), .e(out_10), .d(out_7), .c(out_6));  // open: dp

  assign out_11 = out_8;
endmodule
